# Fritzing sketch Lab3Sketch_H_Bridge (saved by Fritzing 0.8.3b)
breadboards: 1

parts:
  R1 = Resistor [tolerance=±5% resistance=10k package=THT]
  R2 = Resistor [tolerance=±5% resistance=1k package=THT]
  Q1 = PNP-Transistor [part_number=TIP107_Darlington package="TO92 [THT]"]
  Q2 = PNP-Transistor [part_number=TIP107_Darlington package="TO92 [THT]"]
  R3 = Resistor [tolerance=±5% resistance=1k package=THT]
  R4 = Resistor [tolerance=±5% resistance=10k package=THT]
  Q4 = NPN-Transistor [part_number=2N3904 package="TO92 [THT]"]
  R5 = Resistor [tolerance=±5% resistance=10k package=THT]
  R6 = Resistor [tolerance=±5% resistance=10k package=THT]
  R7 = Resistor [tolerance=±5% resistance=1k package=THT]
  R8 = Resistor [tolerance=±5% resistance=1k package=THT]
  Q5 = NPN-Transistor [part_number=TIP102_Darlington package="TO92 [THT]"]
  Q6 = NPN-Transistor [part_number=TIP102_Darlington package="TO92 [THT]"]
  C1 = Ceramic Capacitor [capacitance=100nF package="100 mil [THT, multilayer]"]
  D1 = Rectifier Diode [part_number=1N4936 package="300 mil [THT]"]
  D2 = Rectifier Diode [part_number=1N4936 package="300 mil [THT]"]
  D3 = Rectifier Diode [part_number=1N4936 package="300 mil [THT]"]  # not connected
  D4 = Rectifier Diode [part_number=1N4936 package="300 mil [THT]"]
  LED1 = LED - 5mm [color="Red (633nm)" package="5 mm [THT]"]
  Part1 = Arduino Uno (Rev3)
  LED2 = LED - 5mm [color="Green (570nm)" package="5 mm [THT]"]
  Q3 = NPN-Transistor [part_number=2N3904 package="TO92 [THT]"]
  R9 = Resistor [tolerance=±5% resistance=1k package=THT]
  R10 = Resistor [tolerance=±5% resistance=1k package=THT]
  M1 = DC Motor

nets:
  N1: R1.Pin_0, Q6.B, R10.Pin_0
  N2: R1.Pin_1, Q4.E, R6.Pin_1, Q5.E, Q6.E, D2.anode, D4.anode, Part1.GND, Q3.E
  N3: R2.Pin_0, LED1.cathode
  N4: R2.Pin_1, Q3.B
  N5: Q1.E, Q2.E, R4.Pin_0, R5.Pin_0, D1.cathode, Part1.5V
  N6: Q1.B, R3.Pin_1, R4.Pin_1
  N7: Q1.C, Q5.C, C1.0, D4.cathode, M1.pin_1
  N8: Q2.B, R5.Pin_1, R8.Pin_0
  N9: Q2.C, Q6.C, D1.anode, D2.cathode, M1.pin_2
  N10: R3.Pin_0, Q3.C
  N11: Q4.B, R7.Pin_0
  N12: Q4.C, R8.Pin_1
  N13: R6.Pin_0, Q5.B, R9.Pin_1
  N14: R7.Pin_1, LED2.cathode
  N15: LED1.anode, Part1.D10_PWM/SS, R10.Pin_1
  N16: Part1.D9_PWM, LED2.anode, R9.Pin_0
