# Fritzing sketch fritzing_schematic (saved by Fritzing 0.8.3b)
breadboards: 1

parts:
  Part1 = Arduino Uno (Rev3)
  Q1 = Basic FET P-Channel [package="TO220 [THT]"]
  Q2 = Basic FET N-Channel [package="TO220 [THT]"]
  R1 = Resistor [tolerance=±5% resistance=10k package=THT]
  R2 = Resistor [tolerance=±5% resistance=1k package=THT]
  Q3 = NPN-Transistor [package="TO92 [THT]"]
  R3 = Resistor [tolerance=±5% resistance=1k package=THT]
  R4 = Resistor [tolerance=±5% resistance=10k package=THT]
  R5 = Resistor [tolerance=±5% resistance=1k package=THT]
  D1 = Rectifier Diode [part_number=1N4001 package="300 mil [THT]"]
  D2 = Rectifier Diode [part_number=1N4001 package="300 mil [THT]"]
  Q4 = Basic FET P-Channel [package="TO220 [THT]"]
  Q5 = Basic FET N-Channel [package="TO220 [THT]"]
  R6 = Resistor [tolerance=±5% resistance=10k package=THT]
  R7 = Resistor [tolerance=±5% resistance=1k package=THT]
  Q6 = NPN-Transistor [package="TO92 [THT]"]
  R8 = Resistor [tolerance=±5% resistance=1k package=THT]
  R9 = Resistor [tolerance=±5% resistance=10k package=THT]
  R10 = Resistor [tolerance=±5% resistance=1k package=THT]
  D3 = Rectifier Diode [part_number=1N4001 package="300 mil [THT]"]
  D4 = Rectifier Diode [part_number=1N4001 package="300 mil [THT]"]
  LED1 = LED - 5mm [color="Red (633nm)" package="5 mm [THT]"]
  LED2 = LED - 5mm [color="Green (560nm)" package="5 mm [THT]"]
  C1 = Tantalum Capacitor [capacitance="1 μF" package="100 mil [THT, tantalum]"]
  M1 = DC Motor

nets:
  N1: Part1.GND, Q2.source, Q3.E, R4.Pin_1, D1.anode, Q5.source, Q6.E, R9.Pin_1, D3.anode
  N2: Part1.D9_PWM, LED1.anode
  N3: Part1.D10_PWM/SS, LED2.anode
  N4: Part1.5V, Q1.source, R1.Pin_0, R2.Pin_1, D2.cathode, Q4.source, R6.Pin_0, R7.Pin_1, D4.cathode
  N5: Q1.gate, R1.Pin_1
  N6: Q1.drain, Q2.drain, D1.cathode, D2.anode
  N7: Q2.gate, R4.Pin_0, R5.Pin_1
  N8: R2.Pin_0, Q3.C
  N9: Q3.B, R3.Pin_0, LED1.cathode
  N10: Q4.gate, R6.Pin_1
  N11: Q4.drain, Q5.drain, D3.cathode, D4.anode, C1.+, M1.pin_1
  N12: Q5.gate, R9.Pin_0, R10.Pin_1
  N13: R7.Pin_0, Q6.C
  N14: Q6.B, R8.Pin_0, LED2.cathode
  N15: C1.-, M1.pin_2
