# Fritzing sketch Lab3 (saved by Fritzing 0.8.3b)
breadboards: 1

parts:
  Part1 = Arduino Uno (Rev3)
  Q2 = NPN-Transistor [package="TO92 [THT]"]
  D1 = Rectifier Diode [part_number=1N4936 package="300 mil [THT]"]
  M1 = DC Motor
  Q3 = Basic FET P-Channel [package="TO220 [THT]"]
  R1 = Resistor [tolerance=±5% resistance=1k package=THT]
  R2 = Resistor [tolerance=±5% resistance=10k package=THT]
  LED1 = LED - 5mm [color="Red (633nm)" package="5 mm [THT]"]
  R3 = Resistor [tolerance=±5% resistance=1k package=THT]
  C1 = Ceramic Capacitor [capacitance=0.1µF package="100 mil [THT, multilayer]"]
  Q4 = Basic FET N-Channel [package="TO220 [THT]"]
  R4 = Resistor [tolerance=±5% resistance=1k package=THT]
  D2 = Rectifier Diode [part_number=1N4936 package="300 mil [THT]"]
  R5 = Resistor [tolerance=±5% resistance=10k package=THT]
  Q5 = NPN-Transistor [package="TO92 [THT]"]
  D3 = Rectifier Diode [part_number=1N4936 package="300 mil [THT]"]
  Q6 = Basic FET P-Channel [package="TO220 [THT]"]
  R6 = Resistor [tolerance=±5% resistance=1k package=THT]
  R7 = Resistor [tolerance=±5% resistance=1k package=THT]
  R8 = Resistor [tolerance=±5% resistance=10k package=THT]
  LED2 = LED - 5mm [color="Green (555nm)" package="5 mm [THT]"]
  D4 = Rectifier Diode [part_number=1N4936 package="300 mil [THT]"]
  R9 = Resistor [tolerance=±5% resistance=1k package=THT]
  R10 = Resistor [tolerance=±5% resistance=10k package=THT]
  Q7 = Basic FET N-Channel [package="TO220 [THT]"]

nets:
  N1: Part1.GND, Q2.E, Q4.source, D2.anode, R5.Pin_0, Q5.E, D4.anode, R10.Pin_0, Q7.source
  N2: Part1.D9_PWM, R4.Pin_0, LED2.anode
  N3: Part1.D10_PWM/SS, LED1.anode, R9.Pin_0
  N4: Q2.B, R3.Pin_1
  N5: Q2.C, R1.Pin_0
  N6: D1.cathode, Q3.source, R2.Pin_0, D3.cathode, Q6.source, R8.Pin_0
  N7: D1.anode, M1.pin_1, Q3.drain, C1.1, Q4.drain, D2.cathode
  N8: M1.pin_2, C1.0, D3.anode, Q6.drain, D4.cathode, Q7.drain
  N9: Q3.gate, R1.Pin_1, R2.Pin_1
  N10: LED1.cathode, R3.Pin_0
  N11: Q4.gate, R4.Pin_1, R5.Pin_1
  N12: Q5.B, R6.Pin_1
  N13: Q5.C, R7.Pin_0
  N14: Q6.gate, R7.Pin_1, R8.Pin_1
  N15: R6.Pin_0, LED2.cathode
  N16: R9.Pin_1, R10.Pin_1, Q7.gate
