# Fritzing sketch H_bridge (saved by Fritzing 0.8.3b)
breadboards: 1

parts:
  Q1 = PNP-Transistor [part_number=TIP107 package="TO92 [THT]"]
  Q2 = NPN-Transistor [part_number=TIP102 package="TO92 [THT]"]
  R2 = Resistor [tolerance=±5% resistance=10k package=THT]
  R3 = Resistor [tolerance=±5% resistance=1k package=THT]
  R4 = Resistor [tolerance=±5% resistance=1k package=THT]
  R5 = Resistor [tolerance=±5% resistance=10k package=THT]
  D1 = Rectifier Diode [part_number=1N4936 package="300 mil [THT]"]
  D2 = Rectifier Diode [part_number=1N4936 package="300 mil [THT]"]
  Q3 = NPN-Transistor [part_number=2N3904 package="TO92 [THT]"]
  R6 = Resistor [tolerance=±5% resistance=1k package=THT]
  LED1 = LED - 5mm [color="Red (633nm)" package="5 mm [THT]"]
  Q4 = NPN-Transistor [package="TO92 [THT]"]
  Q5 = PNP-Transistor [package="TO92 [THT]"]
  R7 = Resistor [tolerance=±5% resistance=1k package=THT]
  Q6 = NPN-Transistor [part_number=2N3904 package="TO92 [THT]"]
  R8 = Resistor [tolerance=±5% resistance=10k package=THT]
  D3 = Rectifier Diode [part_number=1N4936 package="300 mil [THT]"]
  D4 = Rectifier Diode [part_number=1N4936 package="300 mil [THT]"]
  R9 = Resistor [tolerance=±5% resistance=10k package=THT]
  R10 = Resistor [tolerance=±5% resistance=1k package=THT]
  R11 = Resistor [tolerance=±5% resistance=220 package=THT]
  LED2 = RGB LED (com. anode, rbg) [package="5 mm [THT]"]
  M1 = DC Motor [part_number="TAMIYA 240"]
  C1 = Ceramic Capacitor [capacitance=100nF package="100 mil [THT, multilayer]"]
  Part1 = Arduino Uno (Rev3)

nets:
  N1: Q1.E, Q2.C, D1.anode, D2.cathode, M1.pin_1, C1.1
  N2: Q1.B, R3.Pin_1, R5.Pin_0
  N3: Q1.C, R5.Pin_1, D1.cathode, Q5.E, D4.cathode, R9.Pin_0, Part1.5V
  N4: Q2.E, R2.Pin_0, D2.anode, Q3.E, Q4.C, Q6.E, R8.Pin_1, D3.anode, Part1.GND
  N5: Q2.B, R2.Pin_1, R4.Pin_1
  N6: R3.Pin_0, Q3.C
  N7: R4.Pin_0, LED2.common_anode
  N8: Q3.B, R6.Pin_1
  N9: R6.Pin_0, LED1.cathode
  N10: LED1.anode, R7.Pin_1
  N11: Q4.E, Q5.C, D3.cathode, D4.anode, M1.pin_2, C1.0
  N12: Q4.B, R7.Pin_0, R8.Pin_0
  N13: Q5.B, R9.Pin_1, R10.Pin_0
  N14: Q6.B, R11.Pin_0
  N15: Q6.C, R10.Pin_1
  N16: R11.Pin_1, LED2.green_cathode
