# Fritzing sketch H_bridge_2 (saved by Fritzing 0.8.3b)
breadboards: 1

parts:
  Part1 = Arduino Uno (Rev3)
  Q1 = pnp-Powertransistor [package="TO220 [THT]"]
  Q2 = pnp-Powertransistor [package="TO220 [THT]"]
  D1 = Rectifier Diode [part_number=1N4001 package="300 mil [THT]"]
  D2 = Rectifier Diode [part_number=1N4001 package="300 mil [THT]"]
  R1 = Resistor [tolerance=±5% resistance=1k package=THT]
  R2 = Resistor [tolerance=±5% resistance=1k package=THT]
  R3 = Resistor [tolerance=±5% resistance=10k package=THT]
  R4 = Resistor [tolerance=±5% resistance=10k package=THT]
  Q3 = NPN-Transistor [package="TO92 [THT]"]
  R5 = Resistor [tolerance=±5% resistance=1k package=THT]
  Q4 = NPN-Transistor [package="TO92 [THT]"]
  R6 = Resistor [tolerance=±5% resistance=1k package=THT]
  LED1 = LED - 5mm [color="Red (633nm)" package="5 mm [THT]"]
  LED2 = LED - 5mm [color="Green (570nm)" package="5 mm [THT]"]
  Q5 = npn-Powertransistor [package="TO220 [THT]"]
  Q6 = npn-Powertransistor [package="TO220 [THT]"]
  D3 = Rectifier Diode [part_number=1N4001 package="300 mil [THT]"]
  D4 = Rectifier Diode [part_number=1N4001 package="300 mil [THT]"]
  R7 = Resistor [tolerance=±5% resistance=1k package=THT]
  R8 = Resistor [tolerance=±5% resistance=10k package=THT]
  R9 = Resistor [tolerance=±5% resistance=1k package=THT]
  R10 = Resistor [tolerance=±5% resistance=10k package=THT]
  M1 = DC Motor
  C1 = Ceramic Capacitor [capacitance=100nF package="100 mil [THT, multilayer]"]  # not connected

nets:
  N1: Part1.GND, Q3.E, Q4.E, Q5.emitter, Q6.emitter, D3.anode, D4.anode, R8.Pin_0, R10.Pin_0
  N2: Part1.D9_PWM, LED2.anode
  N3: Part1.D10_PWM/SS, LED1.anode
  N4: Part1.5V, Q1.emitter, Q2.emitter, D1.cathode, D2.cathode, R3.Pin_0, R4.Pin_0
  N5: Q1.base, R1.Pin_1, R3.Pin_1
  N6: Q1.collector, D1.anode, Q5.collector, D3.cathode, M1.pin_1
  N7: Q2.base, R2.Pin_1, R4.Pin_1
  N8: Q2.collector, D2.anode, Q6.collector, D4.cathode, M1.pin_2
  N9: R1.Pin_0, Q3.C
  N10: R2.Pin_0, Q4.C
  N11: Q3.B, R5.Pin_1
  N12: R5.Pin_0, LED1.cathode
  N13: Q4.B, R6.Pin_1
  N14: R6.Pin_0, LED2.cathode
  N15: Q5.base, R7.Pin_1, R8.Pin_1
  N16: Q6.base, R9.Pin_1, R10.Pin_1
