# Fritzing sketch lab3 (saved by Fritzing 0.8.3b)
breadboards: 1

parts:
  Part1 = Arduino Uno (Rev3)
  Q1 = PNP-Transistor [package="TO92 [THT]"]
  Q2 = NPN-Transistor [package="TO92 [THT]"]
  R1 = Resistor [tolerance=±5% resistance=10k package=THT]
  Q3 = NPN-Transistor [package="TO92 [THT]"]
  R2 = Resistor [tolerance=±5% resistance=1k package=THT]
  R3 = Resistor [tolerance=±5% resistance=1k package=THT]
  LED1 = LED - 5mm [color="Red (633nm)" package="5 mm [THT]"]
  R4 = Resistor [tolerance=±5% resistance=10k package=THT]
  R5 = Resistor [tolerance=±5% resistance=1k package=THT]
  Q4 = PNP-Transistor [package="TO92 [THT]"]
  Q5 = NPN-Transistor [package="TO92 [THT]"]
  R6 = Resistor [tolerance=±5% resistance=10k package=THT]
  R7 = Resistor [tolerance=±5% resistance=10k package=THT]
  Q6 = NPN-Transistor [package="TO92 [THT]"]
  R8 = Resistor [tolerance=±5% resistance=1k package=THT]
  R9 = Resistor [tolerance=±5% resistance=1k package=THT]
  R10 = Resistor [tolerance=±5% resistance=1k package=THT]
  LED2 = LED - 5mm [color="Red (633nm)" package="5 mm [THT]"]
  R11 = Rotary Potentiometer (Small)
  D1 = Rectifier Diode [part_number=1N4001 package="300 mil [THT]"]
  D2 = Rectifier Diode [part_number=1N4001 package="300 mil [THT]"]
  D3 = Rectifier Diode [part_number=1N4001 package="300 mil [THT]"]
  D4 = Rectifier Diode [part_number=1N4001 package="300 mil [THT]"]
  C1 = Ceramic Capacitor [capacitance=100nF package="100 mil [THT, multilayer]"]

nets:
  N1: Part1.GND, Q2.E, Q3.E, R4.Pin_0, Q5.E, R6.Pin_0, Q6.E, D1.cathode, D3.anode
  N2: Part1.D9_PWM, R5.Pin_1, LED2.cathode
  N3: Part1.D10_PWM/SS, LED1.cathode, R10.Pin_1
  N4: Part1.3V3, Q1.C, R1.Pin_0, Q4.C, R7.Pin_0, D2.anode, D4.cathode
  N5: Q1.E, Q2.C, R11.leg1, D1.anode, C1.0
  N6: Q1.B, R1.Pin_1, R2.Pin_1
  N7: Q2.B, R4.Pin_1, R5.Pin_0
  N8: Q3.B, R3.Pin_1
  N9: Q3.C, R2.Pin_0
  N10: R3.Pin_0, LED1.anode
  N11: Q4.E, Q5.C, R11.leg2, D3.cathode, D4.anode, C1.1
  N12: Q4.B, R7.Pin_1, R9.Pin_1
  N13: Q5.B, R6.Pin_1, R10.Pin_0
  N14: Q6.B, R8.Pin_1
  N15: Q6.C, R9.Pin_0
  N16: R8.Pin_0, LED2.anode
