# Fritzing sketch hbridge (saved by Fritzing 0.8.3b)
breadboards: 1

parts:
  Part1 = Arduino Uno (Rev3)
  M1 = DC Motor
  Q1 = Basic FET P-Channel [package="TO220 [THT]"]
  Q2 = Basic FET P-Channel [package="TO220 [THT]"]
  Q3 = Basic FET N-Channel [package="TO220 [THT]"]
  LED1 = LED - 5mm [color="Red (633nm)" package="5 mm [THT]"]
  LED2 = LED - 5mm [color="Green (560nm)" package="5 mm [THT]"]
  R1 = Resistor [tolerance=±5% resistance=10k package=THT]
  D1 = Rectifier Diode [part_number=1N4001 package="300 mil [THT]"]
  C1 = Ceramic Capacitor [capacitance=100nF package="100 mil [THT, multilayer]"]
  D2 = Rectifier Diode [part_number=1N4001 package="300 mil [THT]"]
  D3 = Rectifier Diode [part_number=1N4001 package="300 mil [THT]"]
  D4 = Rectifier Diode [part_number=1N4001 package="300 mil [THT]"]
  R2 = Resistor [tolerance=±5% resistance=10k package=THT]
  Q4 = NPN-Transistor [package="TO92 [THT]"]
  R3 = Resistor [tolerance=±5% resistance=1k package=THT]
  R4 = Resistor [tolerance=±5% resistance=1k package=THT]
  R5 = Resistor [tolerance=±5% resistance=1k package=THT]
  Q5 = NPN-Transistor [package="TO92 [THT]"]
  R6 = Resistor [tolerance=±5% resistance=1k package=THT]
  VCC1 = Battery
  Q6 = Basic FET N-Channel [package="TO220 [THT]"]
  R7 = Resistor [tolerance=±5% resistance=1k package=THT]
  R8 = Resistor [tolerance=±5% resistance=1k package=THT]
  R9 = Resistor [tolerance=±5% resistance=10k package=THT]
  R10 = Resistor [tolerance=±5% resistance=10k package=THT]

nets:
  N1: Part1.GND, D3.anode, Q4.E, Q5.E, VCC1.-, Q6.source, R9.Pin_0, R10.Pin_0
  N2: Part1.D9_PWM, LED1.anode, R8.Pin_1
  N3: Part1.D10_PWM/SS, LED2.anode, R7.Pin_1
  N4: M1.pin_1, Q1.drain, Q3.drain, C1.1, D4.cathode
  N5: M1.pin_2, Q2.drain, D1.anode, C1.0, D3.cathode, Q6.drain
  N6: Q1.gate, R2.Pin_0, R5.Pin_0
  N7: Q1.source, Q2.source, R1.Pin_1, D1.cathode, D2.cathode, D4.anode, R2.Pin_1, VCC1.+
  N8: Q2.gate, R1.Pin_0, R3.Pin_0
  N9: Q3.gate, R8.Pin_0, R9.Pin_1
  N10: LED1.cathode, R4.Pin_1
  N11: LED2.cathode, R6.Pin_1
  N12: Q4.B, R4.Pin_0
  N13: Q4.C, R3.Pin_1
  N14: R5.Pin_1, Q5.C
  N15: Q5.B, R6.Pin_0
  N16: Q6.gate, R7.Pin_0, R10.Pin_1
